# Fritzing sketch ar12_fnd(1) (saved by Fritzing 0.9.3b)
breadboards: 1

parts:
  부품1 = Arduino Uno (Rev3)
  7_Segment1 = 7 Segment Display
  R1 = Resistor [tolerance=±5% resistance=220 package=THT]
  R2 = Resistor [tolerance=±5% resistance=220 package=THT]
  R3 = Resistor [tolerance=±5% resistance=220 package=THT]
  R4 = Resistor [tolerance=±5% resistance=220 package=THT]
  R5 = Resistor [tolerance=±5% resistance=220 package=THT]
  R6 = Resistor [tolerance=±5% resistance=220 package=THT]
  R9 = Resistor [tolerance=±5% resistance=220 package=THT]
  R10 = Resistor [tolerance=±5% resistance=220 package=THT]
  R11 = Resistor [tolerance=±5% resistance=220 package=THT]
  R12 = Resistor [tolerance=±5% resistance=220 package=THT]

nets:
  N1: 부품1.D8, R4.Pin_1
  N2: 부품1.D9_PWM, R11.Pin_0, R12.Pin_0
  N3: 부품1.GND, 7_Segment1.common_anode
  N4: 부품1.D2, R6.Pin_1
  N5: 부품1.D3_PWM, R1.Pin_1
  N6: 부품1.D4, R2.Pin_0, R3.Pin_0
  N7: 부품1.D5_PWM, R10.Pin_0
  N8: 부품1.D6_PWM, R9.Pin_0
  N9: 부품1.D7, R5.Pin_1
  N10: 7_Segment1.Segment_G, R5.Pin_0
  N11: 7_Segment1.Segment_F, R4.Pin_0
  N12: 7_Segment1.Segment_E, R9.Pin_1
  N13: 7_Segment1.Segment_D, R10.Pin_1
  N14: 7_Segment1.Segment_DP, R11.Pin_1, R12.Pin_1
  N15: 7_Segment1.Segment_C, R2.Pin_1, R3.Pin_1
  N16: 7_Segment1.Segment_B, R1.Pin_0
  N17: 7_Segment1.Segment_A, R6.Pin_0
