# Fritzing sketch AR12_4LED (saved by Fritzing 0.9.3b)
breadboards: 1

parts:
  부품1 = Arduino Uno (Rev3)
  R1 = Resistor [tolerance=±5% resistance=220 package=THT]
  R2 = Resistor [tolerance=±5% resistance=220 package=THT]
  LED1 = LED - 5mm [color="Blue (505nm)" package="5 mm [THT]"]  # not connected
  LED2 = LED - 5mm [color="Green (565nm)" package="5 mm [THT]"]
  LED3 = LED - 5mm [color="Yellow (595nm)" package="5 mm [THT]"]
  R3 = Resistor [tolerance=±5% resistance=220 package=THT]
  R4 = Resistor [tolerance=±5% resistance=220 package=THT]
  LED4 = LED - 5mm [color="Red (633nm)" package="5 mm [THT]"]

nets:
  N1: 부품1.D9_PWM, LED3.anode
  N2: 부품1.D3_PWM, LED4.anode
  N3: 부품1.D5_PWM, LED2.anode
  N4: 부품1.GND, R1.Pin_1, R2.Pin_0, R3.Pin_1, R4.Pin_1
  N5: R2.Pin_1, LED2.cathode
  N6: LED3.cathode, R3.Pin_0
  N7: R4.Pin_0, LED4.cathode
