# Fritzing sketch AR12_RGB (saved by Fritzing 0.9.3b)
breadboards: 1

parts:
  부품1 = Arduino Uno (Rev3)
  R1 = Resistor [tolerance=±5% resistance=220 package=THT]
  R2 = Resistor [tolerance=±5% resistance=220 package=THT]
  R3 = Resistor [tolerance=±5% resistance=220 package=THT]
  LED1 = RGB LED (com. cathode, rgb) [package="5 mm [THT]"]

nets:
  N1: 부품1.GND, LED1.common_cathode
  N2: 부품1.D3_PWM, R2.Pin_1
  N3: 부품1.D5_PWM, R1.Pin_1
  N4: 부품1.D6_PWM, R3.Pin_1
  N5: R1.Pin_0, LED1.green_anode
  N6: R2.Pin_0, LED1.red_anode
  N7: R3.Pin_0, LED1.blue_anode
